// Logisim project project-1.circ as structural Verilog: 16 circuits, main circuit main
module main (
  input  in_1,
  input  in_2,
  input  in_3,
  input  in_4,
  input  in_5,
  input  in_6,
  input  in_7,
  input  in_8,
  input  in_9,
  input  in_10,
  input  in_11,
  input  in_12,
  input  in_13,
  input  in_14
);

  wire Clock, DrALU, DrIMM, DrMEM, DrPC, DrREG, DrTarget, LdA, LdB, LdIR, LdMAR, LdPC, LdZ, n0_1_dout,
       reset_splitter_1_resir, ResZ, WrMEM, WrREG, Z;
  wire [1:0] control_unit_1_res, control_unit_1_wr;
  wire [2:0] func;
  wire [4:0] regno;
  wire [5:0] control_unit_1_dr, control_unit_1_ld;
  wire [15:0] control_unit_1_immedout;
  wire [25:0] control_unit_1_targetout;
  wire [31:0] A_dout, alu_32_1_out, B_dout, controlled_buffer_1_out, immediate_sign_extend_1_dout, MAR_dout,
       memory_1_dout, myir_1_dout, PC_dout, register_file_1_dout, target_sign_extend_1_dout;

  Clock clock_1 (.out(Clock));
  myRegister PC (.Din(controlled_buffer_1_out), .LdREG(LdPC), .Clock(Clock), .Dout(PC_dout));
  assign controlled_buffer_1_out = DrPC ? PC_dout : 32'bz;  // Controlled_Buffer controlled_buffer_1
  _0 u_0_1 (.Din(controlled_buffer_1_out), .Dout(n0_1_dout));
  myRegister A (.Din(controlled_buffer_1_out), .LdREG(LdA), .Clock(Clock), .Dout(A_dout));
  Register #(.width(1)) u_Z (.D(n0_1_dout), .en(LdZ), .Q(Z), .clk(Clock), .clr(ResZ));
  ALU_32 alu_32_1 (.A(A_dout), .B(B_dout), .out(alu_32_1_out), .func(func));
  assign controlled_buffer_1_out = DrALU ? alu_32_1_out : 32'bz;  // Controlled_Buffer controlled_buffer_2
  myRegister B (.Din(controlled_buffer_1_out), .LdREG(LdB), .Clock(Clock), .Dout(B_dout));
  Register_File register_file_1 (
    .Din(controlled_buffer_1_out), .WrREG(WrREG), .regno(regno), .Clock(Clock), .Dout(register_file_1_dout));
  assign controlled_buffer_1_out = DrREG ? register_file_1_dout : 32'bz;  // Controlled_Buffer controlled_buffer_3
  myRegister MAR (.Din(controlled_buffer_1_out), .LdREG(LdMAR), .Clock(Clock), .Dout(MAR_dout));
  Memory memory_1 (.Din(controlled_buffer_1_out), .WrMEM(WrMEM), .addr(MAR_dout), .Clock(Clock), .Dout(memory_1_dout));
  assign controlled_buffer_1_out = DrMEM ? memory_1_dout : 32'bz;  // Controlled_Buffer controlled_buffer_4
  Immediate_Sign_Extend immediate_sign_extend_1 (.Din(control_unit_1_immedout), .Dout(immediate_sign_extend_1_dout));
  assign controlled_buffer_1_out = DrIMM ? immediate_sign_extend_1_dout : 32'bz;  // Controlled_Buffer controlled_buffer_5
  myIR myir_1 (
    .Din(controlled_buffer_1_out), .LdREG(LdIR), .Clock(Clock), .Dout(myir_1_dout),
    .in_4(reset_splitter_1_resir));
  Control_Unit control_unit_1 (
    .Din(myir_1_dout), .Dr(control_unit_1_dr), .Ld(control_unit_1_ld), .Wr(control_unit_1_wr), .func(func),
    .regno(regno), .ImmedOUT(control_unit_1_immedout), .TargetOUT(control_unit_1_targetout), .Z(Z),
    .Res(control_unit_1_res), .Clock(Clock));
  Drive_Splitter drive_splitter_1 (
    .Din(control_unit_1_dr), .DrPC(DrPC), .DrALU(DrALU), .DrREG(DrREG), .DrMEM(DrMEM), .DrIMM(DrIMM),
    .DrTARGET(DrTarget));
  Reset_Splitter reset_splitter_1 (.Din(control_unit_1_res), .ResIR(reset_splitter_1_resir), .ResZ(ResZ));
  Target_Sign_Extend target_sign_extend_1 (.Din(control_unit_1_targetout), .Dout(target_sign_extend_1_dout));
  assign controlled_buffer_1_out = DrTarget ? target_sign_extend_1_dout : 32'bz;  // Controlled_Buffer controlled_buffer_6
  Load_Splitter load_splitter_1 (
    .Din(control_unit_1_ld), .LdA(LdA), .LdB(LdB), .LdMAR(LdMAR), .LdIR(LdIR), .LdZ(LdZ), .LdPC(LdPC));
  Write_Splitter write_splitter_1 (.Din(control_unit_1_wr), .WrMEM(WrMEM), .WrREG(WrREG));

  // Other names for the same wires on the sheet: DrALU_t = in_3; DrIMM_t = in_13; DrMEM_t = in_10; DrPC_t = in_2;
  //   DrREG_t = in_6; DrTarget_t = in_14; LdA_t = in_4; LdB_t = in_5; LdIR_t = in_11; LdMAR_t = in_8; LdPC_t = in_1;
  //   LdZ_t = in_12; WrMEM_t = in_9; WrREG_t = in_7
endmodule

// ALU
module ALU_32 (
  input  [2:0] func,
  input  [31:0] A,
  input  [31:0] B,
  output [31:0] out
);

  wire [31:0] adder_1_out, adder_2_out, and_1_out, multiplier_1_out, or_1_out, shifter_1_out, shifter_2_out,
       subtractor_1_out;

  Adder #(.width(32)) adder_1 (.a(A), .b(B), .out(adder_1_out));  // open: cin, cout
  Adder #(.width(32)) adder_2 (.a(A), .b(32'h1), .out(adder_2_out));  // open: cin, cout
  Subtractor #(.width(32)) subtractor_1 (.a(A), .b(B), .out(subtractor_1_out));  // open: bin, bout
  Multiplier #(.width(32)) multiplier_1 (.a(A), .b(B), .out(multiplier_1_out));  // open: cin, cout
  Shifter #(.width(32)) shifter_1 (.in(A), .\dist (B[4:0]), .out(shifter_1_out));
  Shifter #(.width(32), .shift("lr")) shifter_2 (.in(A), .\dist (B[4:0]), .out(shifter_2_out));
  assign and_1_out = A & B;  // AND_Gate and_1, 32 bits wide
  assign or_1_out = A | B;  // OR_Gate or_1, 32 bits wide
  Multiplexer #(.select(3), .width(32), .enable("false")) multiplexer_1 (
    .in0(adder_1_out), .in1(adder_2_out), .in2(subtractor_1_out), .in3(multiplier_1_out),
    .in4(shifter_1_out), .in5(shifter_2_out), .in6(and_1_out), .in7(or_1_out), .out(out), .sel(func));

  // Notes on the sheet:
  //   Adder-32
  //   A + 1
  //   A - B
  //   Mult
  //   Shift Left
  //   Shift Right
  //   AND-32
  //   OR-32
endmodule

// Register File \n 32 x 32 bits
module Register_File (
  input  [31:0] Din,
  input  WrREG,
  input  [4:0] regno,
  input  Clock,
  output [31:0] Dout
);

  wire not_1_out;

  assign Dout = WrREG ? Din : 32'bz;  // Controlled_Buffer controlled_buffer_1
  not not_1 (not_1_out, WrREG);
  RAM #(.addrWidth(5), .dataWidth(32)) ram_1 (
    .addr(regno), .data(Dout), .clk(Clock), .ld(not_1_out));  // open: sel, clr
  RAM #(.addrWidth(5), .dataWidth(32)) ram_2 ();  // open: addr, data, sel, clk, ld, clr
endmodule

// Reg
module myRegister (
  input  [31:0] Din,
  input  LdREG,
  input  Clock,
  output [31:0] Dout
);

  Register #(.width(32)) register_1 (.D(Din), .en(LdREG), .Q(Dout), .clk(Clock));  // open: clr
endmodule

// Memory\n2^24 x 32 bits
module Memory (
  input  [31:0] Din,
  input  WrMEM,
  input  [31:0] addr,
  input  Clock,
  output [31:0] Dout
);

  wire not_1_out;

  assign Dout = WrMEM ? Din : 32'bz;  // Controlled_Buffer controlled_buffer_1
  not not_1 (not_1_out, WrMEM);
  RAM #(.addrWidth(24), .dataWidth(32)) ram_1 (
    .addr(addr[23:0]), .data(Dout), .clk(Clock), .ld(not_1_out));  // open: sel, clr
endmodule

module Control_Unit (
  input  [31:0] Din,
  input  Clock,
  input  Z,
  output [5:0] Dr,
  output [5:0] Ld,
  output [1:0] Wr,
  output [1:0] Res,
  output [2:0] func,
  output [4:0] regno,
  output [15:0] ImmedOUT,
  output [25:0] TargetOUT
);

  wire and_1_out, halt_detection_1_halt_out, not_1_out;
  wire [1:0] rom_1_data_2;
  wire [4:0] rom_1_data, state_register_1_dout;

  Multiplexer #(.select(2), .width(5)) multiplexer_1 (
    .in0(Din[25:21]), .in1(Din[20:16]), .in2(Din[15:11]), .in3({5{1'b1}}), .out(regno), .sel(rom_1_data_2));  // open: en
  State_Register state_register_1 (.Din(rom_1_data), .Clock(and_1_out), .Dout(state_register_1_dout), .clr(Res[1]));
  ROM #(.addrWidth(12), .dataWidth(26)) rom_1 (
    .addr({Din[31:26], Z, state_register_1_dout}), .data({Dr, Ld, Wr, Res, func, rom_1_data_2, rom_1_data}));  // open: sel
  and and_1 (and_1_out, Clock, not_1_out);
  not not_1 (not_1_out, halt_detection_1_halt_out);
  Halt_Detection halt_detection_1 (
    .Reset_In(Res), .Next_State_In(rom_1_data), .Func_In(func), .Halt_Out(halt_detection_1_halt_out));

  assign ImmedOUT = Din[15:0];
  assign TargetOUT = Din[25:0];

  // Notes on the sheet:
  //   Registers (b25-b11)
  //   opcode (b31-b26)
  //   Target Address (b25-b0)
  //    (b10-b0)
  //   Src A (b25-b21)
  //   dest (b15-b11)
  //   (b15-b0)
  //   Ld: PC, A, B, MAR, IR
  //   contents of rom_1 (hex, n*v repeats v):
  //   2050001 1080082 408000 61*0 840001 820022 1001043 800 60*0 840001 220022 1001023 800 60*0 840001
  //   820022 10011c3 800 60*0 840001 220022 1001223 800 60*0 840001 220022 10012a3 800 60*0 840001 820022
  //   1001343 800 60*0 840001 820022 10013c3 800 60*0 840001 220002 1010003 401024 800 59*0 840001 220002
  //   1010003 802024 800 59*0 180001 800 62*0 880001 800 62*0 2001061 180002 800 61*0 840001 820022
  //   1004103 c07 31*0 2040004 220005 1080006 c07 25*0 79f
  //   Next State (b0-b4)
  //   Dr: pc, alu, reg, mem, ImmOff, targOff 
  //   Immediate (b15-b0)
  //   Taget Address (b25-b0)
  //   Reg Sel (b6-b5)
  //   (b25-b20
  //   (b19-b14)
  //   (b13-b12)
  //   (b11-b10)
  //   (b9-b7)
endmodule

module _0 (
  input  [31:0] Din,
  output Dout
);

  wire and_1_out, and_2_out, nor_1_out, nor_2_out, nor_3_out, nor_4_out, nor_5_out, nor_6_out, nor_7_out,
       nor_8_out;

  nor nor_1 (nor_1_out, Din[0], Din[1], Din[2], Din[3]);
  nor nor_2 (nor_2_out, Din[4], Din[5], Din[6], Din[7]);
  nor nor_3 (nor_3_out, Din[8], Din[9], Din[10], Din[11]);
  nor nor_4 (nor_4_out, Din[12], Din[13], Din[14], Din[15]);
  nor nor_5 (nor_5_out, Din[20], Din[21], Din[22], Din[23]);
  nor nor_6 (nor_6_out, Din[24], Din[25], Din[26], Din[27]);
  nor nor_7 (nor_7_out, Din[28], Din[29], Din[30], Din[31]);
  nor nor_8 (nor_8_out, Din[16], Din[17], Din[18], Din[19]);
  and and_1 (and_1_out, nor_1_out, nor_2_out, nor_3_out, nor_4_out);
  and and_2 (and_2_out, nor_8_out, nor_5_out, nor_6_out, nor_7_out);
  and and_3 (Dout, and_1_out, and_2_out);
endmodule

module State_Register (
  input  [4:0] Din,
  input  Clock,
  input  clr,
  output [4:0] Dout
);

  Register #(.width(5)) register_1 (.D(Din), .en(1'b1), .Q(Dout), .clk(Clock), .clr(clr));
endmodule

// 16 bit\nSign \nExtend
module Immediate_Sign_Extend (
  input  [15:0] Din,
  output [31:0] Dout
);

  assign Dout = {{16{Din[15]}}, Din};  // Bit_Extender bit_extender_1
endmodule

// 26 bit \n Sign \n Extend
module Target_Sign_Extend (
  input  [25:0] Din,
  output [31:0] Dout
);

  assign Dout = {{6{Din[25]}}, Din};  // Bit_Extender bit_extender_1
endmodule

// Drive
module Drive_Splitter (
  input  [5:0] Din,
  output DrPC,
  output DrALU,
  output DrREG,
  output DrMEM,
  output DrIMM,
  output DrTARGET
);


  assign DrALU = Din[4];
  assign DrIMM = Din[1];
  assign DrMEM = Din[2];
  assign DrPC = Din[5];
  assign DrREG = Din[3];
  assign DrTARGET = Din[0];
endmodule

// Load
module Load_Splitter (
  input  [5:0] Din,
  output LdPC,
  output LdA,
  output LdB,
  output LdMAR,
  output LdIR,
  output LdZ
);


  assign LdA = Din[4];
  assign LdB = Din[3];
  assign LdIR = Din[1];
  assign LdMAR = Din[2];
  assign LdPC = Din[5];
  assign LdZ = Din[0];
endmodule

// Write
module Write_Splitter (
  input  [1:0] Din,
  output WrMEM,
  output WrREG
);


  assign WrMEM = Din[1];
  assign WrREG = Din[0];
endmodule

// Reset
module Reset_Splitter (
  input  [1:0] Din,
  output ResIR,
  output ResZ
);


  assign ResIR = Din[1];
  assign ResZ = Din[0];
endmodule

// IR
module myIR (
  input  [31:0] Din,
  input  LdREG,
  input  Clock,
  input  in_4,
  output [31:0] Dout
);

  Register #(.width(32)) register_1 (.D(Din), .en(LdREG), .Q(Dout), .clk(Clock), .clr(in_4));
endmodule

// Halt Detect
module Halt_Detection (
  input  [1:0] Reset_In,
  input  [4:0] Next_State_In,
  input  [2:0] Func_In,
  output Halt_Out
);

  wire and_1_out, and_2_out;

  and and_1 (and_1_out, Next_State_In[0], Next_State_In[1], Next_State_In[2], Next_State_In[3], Next_State_In[4]);
  and and_2 (and_2_out, Func_In[0], Func_In[1], Func_In[2]);
  and and_3 (Halt_Out, Reset_In[0], and_1_out, and_2_out);
endmodule
