// Logisim project LC-2200-32-keyboard.circ as structural Verilog: 13 circuits, main circuit Processor
module Processor (
);

  wire Clock, Clr, comparator_1_lt, DrALU, DrKEY, DrMEM, DrOFF, DrPC, DrReg, EnInt, ie_register_1_dout,
       IntAck, intergenerator_1_intout, keyboard_w_interrupt_1_intout, keyInt, KIntAck, LdA, LdB, LdEnInt,
       LdIR, LdMAR, LdPC, LdZ, not_1_out, or_1_out, register_1_q, TimeInt, TIntAck, WrMEM, WrREG, Z,
       ZeroDetectOut;
  wire [1:0] FUNC, RegSel;
  wire [2:0] state_machine_1_intout;
  wire [3:0] Opcode, Reg_num;
  wire [5:0] state_machine_1_drout, state_machine_1_ldout;
  wire [23:0] MAR_q;
  wire [27:0] IR_q;
  wire [31:0] A_q, B_q, controlled_buffer_1_out, intergenerator_1_ivtindex, keyboard_w_interrupt_1_charout,
       keyboard_w_interrupt_1_vecout, multiplexer_1_out, PC_q, ram_1_data, register_2_q,
       registers_1_data_out, ZeroDetect;

  assign controlled_buffer_1_out = DrPC ? multiplexer_1_out : 32'bz;  // Controlled_Buffer controlled_buffer_1
  Clock clock_1 (.out(Clock));
  Button button_1 (.out(Clr));
  Register #(.width(32)) PC (.D(controlled_buffer_1_out), .en(LdPC), .Q(PC_q), .clk(Clock), .clr(Clr));
  Comparator #(.width(32), .mode("unsigned")) comparator_1 (
    .a(PC_q), .b(32'h10), .lt(comparator_1_lt));  // open: gt, eq
  Comparator #(.width(32), .mode("unsigned")) comparator_2 (
    .a(ZeroDetect), .b({32{1'b0}}), .eq(ZeroDetectOut));  // open: gt, lt
  Multiplexer #(.width(32), .enable("false")) multiplexer_1 (
    .in0(PC_q), .in1(32'h10), .out(multiplexer_1_out), .sel(comparator_1_lt));
  Register #(.width(1)) Z_Register (.D(ZeroDetectOut), .en(LdZ), .Q(Z), .clk(Clock), .clr(Clr));
  Register #(.width(32)) A (.D(controlled_buffer_1_out), .en(LdA), .Q(A_q), .clk(Clock), .clr(Clr));
  ALU alu_1 (.FUNC(FUNC), .INPUT_A(A_q), .INPUT_B(B_q), .out_4(ZeroDetect));
  assign controlled_buffer_1_out = DrALU ? ZeroDetect : 32'bz;  // Controlled_Buffer controlled_buffer_2
  assign controlled_buffer_1_out = TIntAck ? intergenerator_1_ivtindex : 32'bz;  // Controlled_Buffer controlled_buffer_3
  Intergenerator intergenerator_1 (.IntOut(intergenerator_1_intout), .CLK(Clock), .IVTindex(intergenerator_1_ivtindex));
  Register #(.width(32)) B (.D(controlled_buffer_1_out), .en(LdB), .Q(B_q), .clk(Clock), .clr(Clr));
  Register #(.width(1)) register_1 (
    .D(intergenerator_1_intout), .en(intergenerator_1_intout), .Q(register_1_q), .clk(Clock), .clr(TIntAck));
  Registers registers_1 (
    .WrReg(WrREG), .RegSel(Reg_num), .Data_In(controlled_buffer_1_out), .Clock(Clock), .ClearRegFile(Clr),
    .Data_Out(registers_1_data_out));
  assign controlled_buffer_1_out = DrReg ? registers_1_data_out : 32'bz;  // Controlled_Buffer controlled_buffer_4
  IE_Register ie_register_1 (.Din(EnInt), .Clock(Clock), .Dout(ie_register_1_dout), .LdEnInt(LdEnInt));
  and and_1 (TimeInt, ie_register_1_dout, register_1_q);
  assign controlled_buffer_1_out = KIntAck ? keyboard_w_interrupt_1_vecout : 32'bz;  // Controlled_Buffer controlled_buffer_5
  Register #(.width(24)) MAR (.D(controlled_buffer_1_out[23:0]), .en(LdMAR), .Q(MAR_q), .clk(Clock), .clr(Clr));
  not not_1 (not_1_out, WrMEM);
  Keyboard_w_Interrupt keyboard_w_interrupt_1 (
    .ClrCHAR(KIntAck), .CharOUT(keyboard_w_interrupt_1_charout), .VecOUT(keyboard_w_interrupt_1_vecout),
    .En(TIntAck), .IntOUT(keyboard_w_interrupt_1_intout));
  and and_2 (keyInt, keyboard_w_interrupt_1_intout, ie_register_1_dout);
  Interrupt_Selector interrupt_selector_1 (
    .TimeInt(register_1_q), .KeyInt(keyboard_w_interrupt_1_intout), .IntAck(IntAck), .KIntAck(KIntAck),
    .TintAck(TIntAck), .Clock(Clock));
  RAM #(.addrWidth(24), .dataWidth(32), .bus("separate")) ram_1 (
    .addr(MAR_q), .din(controlled_buffer_1_out), .data(ram_1_data), .str(WrMEM), .clk(Clock), .ld(not_1_out),
    .clr(Clr));  // open: sel
  assign controlled_buffer_1_out = DrMEM ? ram_1_data : 32'bz;  // Controlled_Buffer controlled_buffer_6
  Register #(.width(32)) register_2 (
    .D(keyboard_w_interrupt_1_charout), .Q(register_2_q), .clk(KIntAck));  // open: en, clr
  assign controlled_buffer_1_out = DrKEY ? register_2_q : 32'bz;  // Controlled_Buffer controlled_buffer_7
  Register #(.width(32)) IR (.D(controlled_buffer_1_out), .en(LdIR), .Q({Opcode, IR_q}), .clk(Clock), .clr(Clr));
  Multiplexer #(.select(2), .width(4), .enable("false")) multiplexer_2 (
    .in0(IR_q[27:24]), .in1(IR_q[23:20]), .in2(IR_q[3:0]), .in3(4'b1100), .out(Reg_num), .sel(RegSel));
  assign controlled_buffer_1_out = DrOFF ? {{13{IR_q[19]}}, IR_q[18:0]} : 32'bz;  // Controlled_Buffer controlled_buffer_8
  or or_1 (or_1_out, keyInt, TimeInt);
  State_Machine state_machine_1 (
    .Clock(Clock), .OpCode(Opcode), .Z(Z), .IntOut(state_machine_1_intout), .ALU_FUNC(FUNC), .RegSel(RegSel),
    .WrOUT({WrMEM, WrREG}), .LdOUT(state_machine_1_ldout), .DrOUT(state_machine_1_drout), .Int(or_1_out));
  Interrupt_Splitter interrupt_splitter_1 (
    .in_1(state_machine_1_intout), .IntAck(IntAck), .EnInt(EnInt), .LdEnInt(LdEnInt));
  Drive_Splitter drive_splitter_1 (
    .in_1(state_machine_1_drout), .DrREG(DrReg), .DrMEM(DrMEM), .DrALU(DrALU), .DrPC(DrPC), .DrOFF(DrOFF),
    .DrKEY(DrKEY));
  Load_Splitter load_splitter_1 (
    .in_1(state_machine_1_ldout), .LdZ(LdZ), .LdB(LdB), .LdA(LdA), .LdMAR(LdMAR), .LdIR(LdIR), .LdPC(LdPC));
  IE_Register ie_register_2 (.Clock(Clock), .LdEnInt(LdEnInt));  // open: Din, Dout

  // Notes on the sheet:
  //   Hold Int
  //   00 = RX
  //   01 = RY
  //   10 = RZ
  //   $k0
endmodule

module ALU (
  input  [31:0] INPUT_B,
  input  [31:0] INPUT_A,
  input  [1:0] FUNC,
  output [31:0] out_4
);

  wire [31:0] adder_1_out, adder_2_out, nand_1_out, subtractor_1_out;

  Adder #(.width(32)) adder_1 (.a(INPUT_A), .b(INPUT_B), .out(adder_1_out));  // open: cin, cout
  assign nand_1_out = ~(INPUT_A & INPUT_B);  // NAND_Gate nand_1, 32 bits wide
  Multiplexer #(.select(2), .width(32), .enable("false")) multiplexer_1 (
    .in0(adder_1_out), .in1(nand_1_out), .in2(subtractor_1_out), .in3(adder_2_out), .out(out_4), .sel(FUNC));
  Subtractor #(.width(32)) subtractor_1 (.a(INPUT_A), .b(INPUT_B), .out(subtractor_1_out));  // open: bin, bout
  Adder #(.width(32)) adder_2 (.a(INPUT_A), .b(32'h1), .out(adder_2_out));  // open: cin, cout
endmodule

// State\n Machine
module State_Machine (
  input  Clock,
  input  [3:0] OpCode,
  input  Z,
  input  Int,
  output [2:0] IntOut,
  output [1:0] ALU_FUNC,
  output [1:0] RegSel,
  output [1:0] WrOUT,
  output [5:0] LdOUT,
  output [5:0] DrOUT
);

  wire chkZ, OpTest;
  wire [5:0] multiplexer_1_out, register_1_q, rom_1_data, rom_2_data, rom_3_data, rom_4_data;

  Register #(.width(6)) register_1 (.D(multiplexer_1_out), .en(Clock), .Q(register_1_q), .clk(Clock));  // open: clr
  Multiplexer #(.select(2), .width(6), .enable("false")) multiplexer_1 (
    .in0(rom_1_data), .in1(rom_2_data), .in2(rom_3_data), .in3(rom_4_data), .out(multiplexer_1_out),
    .sel({chkZ, OpTest}));
  ROM #(.addrWidth(6), .dataWidth(29)) rom_1 (
    .addr(register_1_q),
    .data({DrOUT[5], IntOut, chkZ, OpTest, ALU_FUNC, RegSel, WrOUT, LdOUT, DrOUT[4:0], rom_1_data}));  // open: sel
  ROM #(.addrWidth(4), .dataWidth(6)) rom_2 (.addr(OpCode), .data(rom_2_data));  // open: sel
  ROM #(.addrWidth(2), .dataWidth(6)) rom_3 (.addr({1'b0, Z}), .data(rom_3_data));  // open: sel
  ROM #(.addrWidth(2), .dataWidth(6)) rom_4 (.addr({1'b0, Int}), .data(rom_4_data));  // open: sel

  // Notes on the sheet:
  //   contents of rom_1 (hex, n*v repeats v):
  //   1800001 6202 1083 e00900 21a0205 8002006 880 84048 108049 20100 8404b 10804c 220100 8404e 840f 20100
  //   84051 8412 2113 20080 84055 8416 2117 40040 4059 8805a 41011b 1000000 421d 841e 900 a0220 840
  //   6000000 2000000 6180840 24 10020000
  //   Next State
  //   b0-b5
  //   Interrupt ROM
  //   contents of rom_2 (hex, n*v repeats v):
  //   7 a d 10 14 18 1f 24 0 0 21 22 23 0 25
  //   contents of rom_3 (hex, n*v repeats v):
  //   0 1c
  //   contents of rom_4 (hex, n*v repeats v):
  //   1 4
endmodule

// 0?
module Zero_Detection (
  input  [31:0] In,
  output Out
);

  Comparator #(.width(32), .mode("unsigned")) comparator_1 (.a(In), .b({32{1'b0}}), .eq(Out));  // open: gt, lt
endmodule

// Reg File
module Registers (
  input  [31:0] Data_In,
  input  WrReg,
  input  [3:0] RegSel,
  input  Clock,
  input  ClearRegFile,
  output [31:0] Data_Out
);

  wire and_1_out, and_2_out, and_3_out, and_4_out, and_5_out, and_6_out, and_7_out, and_8_out, and_9_out,
       and_10_out, and_11_out, and_12_out, and_13_out, and_14_out, and_15_out, and_16_out, decoder_1_out0,
       decoder_1_out1, decoder_1_out2, decoder_1_out3, decoder_1_out4, decoder_1_out5, decoder_1_out6,
       decoder_1_out7, decoder_1_out8, decoder_1_out9, decoder_1_out10, decoder_1_out11, decoder_1_out12,
       decoder_1_out13, decoder_1_out14, decoder_1_out15;
  wire [31:0] a0, a1, a2, at, k0, pr, ra, s0, s1, s2, sp, t0, t1, t2, v0, zero;

  Decoder #(.select(4), .enable("false")) decoder_1 (
    .out0(decoder_1_out0), .out1(decoder_1_out1), .out2(decoder_1_out2), .out3(decoder_1_out3),
    .out4(decoder_1_out4), .out5(decoder_1_out5), .out6(decoder_1_out6), .out7(decoder_1_out7),
    .out8(decoder_1_out8), .out9(decoder_1_out9), .out10(decoder_1_out10), .out11(decoder_1_out11),
    .out12(decoder_1_out12), .out13(decoder_1_out13), .out14(decoder_1_out14), .out15(decoder_1_out15),
    .sel(RegSel));
  and and_1 (and_1_out, decoder_1_out0, WrReg);
  and and_2 (and_2_out, decoder_1_out1, WrReg);
  and and_3 (and_3_out, decoder_1_out2, WrReg);
  and and_4 (and_4_out, decoder_1_out3, WrReg);
  and and_5 (and_5_out, decoder_1_out4, WrReg);
  and and_6 (and_6_out, decoder_1_out5, WrReg);
  and and_7 (and_7_out, decoder_1_out6, WrReg);
  and and_8 (and_8_out, decoder_1_out7, WrReg);
  and and_9 (and_9_out, decoder_1_out8, WrReg);
  and and_10 (and_10_out, decoder_1_out9, WrReg);
  and and_11 (and_11_out, decoder_1_out10, WrReg);
  and and_12 (and_12_out, decoder_1_out11, WrReg);
  and and_13 (and_13_out, decoder_1_out12, WrReg);
  and and_14 (and_14_out, decoder_1_out13, WrReg);
  and and_15 (and_15_out, decoder_1_out14, WrReg);
  and and_16 (and_16_out, decoder_1_out15, WrReg);
  Register #(.width(32)) u_zero (.D(Data_In), .en(and_1_out), .Q(zero), .clk(Clock), .clr(1'b1));
  Register #(.width(32)) u_at (.D(Data_In), .en(and_2_out), .Q(at), .clk(Clock), .clr(ClearRegFile));
  Register #(.width(32)) u_v0 (.D(Data_In), .en(and_3_out), .Q(v0), .clk(Clock), .clr(ClearRegFile));
  Register #(.width(32)) u_a0 (.D(Data_In), .en(and_4_out), .Q(a0), .clk(Clock), .clr(ClearRegFile));
  Register #(.width(32)) u_a1 (.D(Data_In), .en(and_5_out), .Q(a1), .clk(Clock), .clr(ClearRegFile));
  Register #(.width(32)) u_a2 (.D(Data_In), .en(and_6_out), .Q(a2), .clk(Clock), .clr(ClearRegFile));
  Register #(.width(32)) u_t0 (.D(Data_In), .en(and_7_out), .Q(t0), .clk(Clock), .clr(ClearRegFile));
  Register #(.width(32)) u_t1 (.D(Data_In), .en(and_8_out), .Q(t1), .clk(Clock), .clr(ClearRegFile));
  Register #(.width(32)) u_t2 (.D(Data_In), .en(and_9_out), .Q(t2), .clk(Clock), .clr(ClearRegFile));
  Register #(.width(32)) u_s0 (.D(Data_In), .en(and_10_out), .Q(s0), .clk(Clock), .clr(ClearRegFile));
  Register #(.width(32)) u_s1 (.D(Data_In), .en(and_11_out), .Q(s1), .clk(Clock), .clr(ClearRegFile));
  Register #(.width(32)) u_s2 (.D(Data_In), .en(and_12_out), .Q(s2), .clk(Clock), .clr(ClearRegFile));
  Register #(.width(32)) u_k0 (.D(Data_In), .en(and_13_out), .Q(k0), .clk(Clock), .clr(ClearRegFile));
  Register #(.width(32)) u_sp (.D(Data_In), .en(and_14_out), .Q(sp), .clk(Clock), .clr(ClearRegFile));
  Register #(.width(32)) u_pr (.D(Data_In), .en(and_15_out), .Q(pr), .clk(Clock), .clr(ClearRegFile));
  Register #(.width(32)) u_ra (.D(Data_In), .en(and_16_out), .Q(ra), .clk(Clock), .clr(ClearRegFile));
  Multiplexer #(.select(4), .width(32), .enable("false")) multiplexer_1 (
    .in0(zero), .in1(at), .in2(v0), .in3(a0), .in4(a1), .in5(a2), .in6(t0), .in7(t1), .in8(t2), .in9(s0),
    .in10(s1), .in11(s2), .in12(k0), .in13(sp), .in14(pr), .in15(ra), .out(Data_Out), .sel(RegSel));

  // Other names for the same wires on the sheet: Din[31:0] = Data_In; en = WrReg
endmodule

// Inter\ngen\nerator
module Intergenerator (
  input  CLK,
  output IntOut,
  output [31:0] IVTindex
);

  wire register_2_q;
  wire [10:0] adder_1_out, register_1_q;

  Adder #(.width(11)) adder_1 (.a(11'h1), .b(register_1_q), .out(adder_1_out));  // open: cin, cout
  Register #(.width(11)) register_1 (.D(adder_1_out), .en(1'b1), .Q(register_1_q), .clk(CLK), .clr(register_2_q));
  Comparator #(.width(11), .mode("unsigned")) comparator_1 (
    .a(11'h200), .b(register_1_q), .eq(IntOut));  // open: gt, lt
  Register #(.width(1)) register_2 (.D(IntOut), .en(1'b1), .Q(register_2_q), .clk(CLK), .clr(register_2_q));

  assign IVTindex = 32'h1;
endmodule

module k0 (
  input  [31:0] Din,
  input  Ld_k0,
  input  Clock_IN,
  output [31:0] Dout
);

  Register #(.width(32)) register_1 (.D(Din), .en(Ld_k0), .Q(Dout), .clk(Clock_IN));  // open: clr
endmodule

// Dr\n Splitter
module Drive_Splitter (
  input  [5:0] in_1,
  output DrREG,
  output DrMEM,
  output DrALU,
  output DrPC,
  output DrOFF,
  output DrKEY
);


  assign DrALU = in_1[2];
  assign DrKEY = in_1[5];
  assign DrMEM = in_1[1];
  assign DrOFF = in_1[4];
  assign DrPC = in_1[3];
  assign DrREG = in_1[0];
endmodule

// Ld\n Splitter
module Load_Splitter (
  input  [5:0] in_1,
  output LdZ,
  output LdB,
  output LdA,
  output LdMAR,
  output LdIR,
  output LdPC
);


  assign LdA = in_1[3];
  assign LdB = in_1[4];
  assign LdIR = in_1[1];
  assign LdMAR = in_1[2];
  assign LdPC = in_1[0];
  assign LdZ = in_1[5];
endmodule

// Int\n Splitter
module Interrupt_Splitter (
  input  [2:0] in_1,
  output IntAck,
  output EnInt,
  output LdEnInt
);


  assign EnInt = in_1[1];
  assign IntAck = in_1[2];
  assign LdEnInt = in_1[0];
endmodule

// EnInt\n Register
module IE_Register (
  input  Din,
  input  LdEnInt,
  input  Clock,
  output Dout
);

  Register #(.width(1)) register_1 (.D(Din), .en(LdEnInt), .Q(Dout), .clk(Clock));  // open: clr
endmodule

// Int\n Sel
module Interrupt_Selector (
  input  TimeInt,
  input  KeyInt,
  input  IntAck,
  input  Clock,
  output KIntAck,
  output TintAck
);

  wire priority_encoder_1_p1, register_1_q, register_2_q, register_3_q;
  wire [1:0] priority_encoder_1_p4;

  Register #(.width(1)) register_1 (
    .D(TimeInt), .Q(register_1_q), .clk(Clock), .clr(priority_encoder_1_p1));  // open: en
  Register #(.width(1)) register_2 (.D(KeyInt), .Q(register_2_q), .clk(Clock), .clr(register_3_q));  // open: en
  // Priority_Encoder #(.select(2)) priority_encoder_1: pin names not known; wires that end beside it: priority_encoder_1_p1, 1'b1, register_2_q, priority_encoder_1_p4, register_1_q
  and and_1 (KIntAck, priority_encoder_1_p4[0], IntAck);
  and and_2 (TintAck, IntAck, priority_encoder_1_p4[1]);
  Register #(.width(1)) register_3 (.D(TintAck), .Q(register_3_q), .clk(Clock));  // open: en, clr
  Register #(.width(1)) register_4 (.D(KIntAck), .Q(priority_encoder_1_p1), .clk(Clock));  // open: en, clr

  // Other names for the same wires on the sheet: clk = Clock

  // Notes on the sheet:
  //   Key Int
  //   Time Int
endmodule

// Keyboard
module Keyboard_w_Interrupt (
  input  ClrCHAR,
  input  En,
  output [31:0] VecOUT,
  output [31:0] CharOUT,
  output IntOUT
);

  wire not_1_out;
  wire [6:0] keyboard_1_data;

  Keyboard keyboard_1 (.clk(ClrCHAR), .re(not_1_out), .avail(IntOUT), .data(keyboard_1_data));  // open: clr
  not not_1 (not_1_out, En);
  assign CharOUT = {{25{1'b0}}, keyboard_1_data};  // Bit_Extender bit_extender_1

  assign VecOUT = 32'h2;
endmodule
