// Logisim project prj-3.circ as structural Verilog: 20 circuits, main circuit main
module main (
);

  wire BEQ_Flush_IT, chk_z, Clock, clock_1_out, Clr, Data_Wr_En, Dest_Rs_A, En_z, Flush, HALT, Jump,
       Jump_Flush_IT, MEM_En, not_1_out, or_1_out, Read_Rd, Reg_WrEn, Swap_R1, Swap_R1_Ex, Swap_R1_Mem,
       Swap_R1_Wb, Swap_R2, Swap_R2_Ex, Swap_R2_Mem, Swap_R2_Wb, Use_IMM, Use_PC, WB_Sel_0, WB_Sel_1;
  wire [1:0] FUNC;
  wire [3:0] D_Read_1, D_Read_2, Dest_Reg, E_Dest_out, fetch_buffer_1_rd_out, fetch_buffer_1_rs_b_out,
       Mem_Dest_out, multiplexer_3_out;
  wire [7:0] ex_buffer_1_opcode_out, Ex_Op, fetch_buffer_1_opcode_out, id_rr_buffer_1_opcode_out,
       id_rr_cntrl_1_opcode_out, Mem_Op, Wb_Op;
  wire [15:0] fetch_buffer_1_offset_out;
  wire [31:0] BEQ_PC, bit_extender_1_out, counter_1_q, D_Out_1, D_Out_1_Ex, D_Out_1_Mem, D_Out_1_Wb, D_Out_2,
       D_Out_2_Ex, D_Out_2_Mem, D_Out_2_Wb, dual_ported_register_file_1_out1,
       dual_ported_register_file_1_out2, E_ALU_out, ex_buffer_1_pc_out, ex_buffer_1_rx_out,
       fetch_buffer_1_pc_out, id_rr_buffer_1_data_r2_out, instruction_memory_1_dout, JALR_PC, Mem_ALU_Out,
       mem_buffer_1_mem_out_out, mem_buffer_1_pc_out, Mem_Out, multiplexer_1_out, multiplexer_4_out,
       multiplexer_5_out, multiplexer_6_out, multiplexer_7_out, Offset, PC_1, pc_1_dout, PC_Out, ToWrite,
       WB_ALU_out;

  Multiplexer #(.select(2), .width(32)) multiplexer_1 (
    .in0(PC_1), .in1(JALR_PC), .in2(BEQ_PC), .out(multiplexer_1_out), .sel({chk_z, Jump}));  // open: in3, en
  PC u_pc_1 (.Din(multiplexer_1_out), .Dout(pc_1_dout), .Clk(Clock), .Clear_PC(Clr));
  _1 u_1_1 (.Din(pc_1_dout), .Dout(PC_1));
  not not_1 (not_1_out, HALT);
  Clock clock_1 (.out(clock_1_out));
  Instruction_Memory instruction_memory_1 (
    .Din(pc_1_dout), .Dout(instruction_memory_1_dout), .Clk(Clock));  // open: Clear_IR
  Counter #(.width(32), .max('hffffffff)) counter_1 (
    .load(1'b0), .count(1'b1), .Q(counter_1_q), .clk(Clock), .clr(Clr));  // open: D, carry
  and and_1 (Clock, not_1_out, clock_1_out);
  Button button_1 (.out(Clr));
  // Probe on counter_1_q
  Fetch_Buffer fetch_buffer_1 (
    .Offset_In(instruction_memory_1_dout[15:0]), .Rs_B_In(instruction_memory_1_dout[15:12]),
    .Rs_A_In(instruction_memory_1_dout[19:16]), .Rd_In(instruction_memory_1_dout[23:20]),
    .OpCode_In(instruction_memory_1_dout[31:24]), .PC_In(PC_1), .Clk_FBuff(Clock),
    .Offset_Out(fetch_buffer_1_offset_out), .Rs_B_Out(fetch_buffer_1_rs_b_out), .Rs_A_Out(D_Read_2),
    .Rd_Out(fetch_buffer_1_rd_out), .Opcode_Out(fetch_buffer_1_opcode_out), .PC_Out(fetch_buffer_1_pc_out),
    .Flush(Flush));
  assign bit_extender_1_out = {{16{fetch_buffer_1_offset_out[15]}}, fetch_buffer_1_offset_out};  // Bit_Extender bit_extender_1
  Multiplexer #(.width(4), .enable("false")) multiplexer_2 (
    .in0(fetch_buffer_1_rs_b_out), .in1(fetch_buffer_1_rd_out), .out(D_Read_1), .sel(Read_Rd));
  Multiplexer #(.width(4), .enable("false")) multiplexer_3 (
    .in0(fetch_buffer_1_rd_out), .in1(D_Read_2), .out(multiplexer_3_out), .sel(Dest_Rs_A));
  ID_RR_Cntrl id_rr_cntrl_1 (
    .Opcode_In(fetch_buffer_1_opcode_out), .Read_Rd(Read_Rd), .Opcode_Out(id_rr_cntrl_1_opcode_out),
    .Dest_Rs_A(Dest_Rs_A));
  Master_Forwarding_Unit master_forwarding_unit_1 (
    .Forward_WB_1_In(Swap_R1_Wb), .Forward_MEM_1_In(Swap_R1_Mem), .Forward_EX_1_In(Swap_R1_Ex),
    .WB_D_1(D_Out_1_Wb), .MEM_D_1(D_Out_1_Mem), .EX_D_1(D_Out_1_Ex), .Forward_WB_2_In(Swap_R2_Wb),
    .Forward_MEM_2_In(Swap_R2_Mem), .Forward_EX_2_In(Swap_R2_Ex), .WB_D_2(D_Out_2_Wb), .MEM_D_2(D_Out_2_Mem),
    .EX_D_2(D_Out_2_Ex), .Swap_R1(Swap_R1), .D_1_Out(D_Out_1), .Swap_R2(Swap_R2), .D_2_Out(D_Out_2));
  Dual_Ported_Register_File dual_ported_register_file_1 (
    .CLK(Clock), .WrREGNO(Dest_Reg), .RdREGNO1(D_Read_1), .RdREGNO2(D_Read_2), .INPUT(ToWrite),
    .OUT1(dual_ported_register_file_1_out1), .OUT2(dual_ported_register_file_1_out2), .WrEN(Reg_WrEn));
  Multiplexer #(.width(32), .enable("false")) multiplexer_4 (
    .in0(dual_ported_register_file_1_out1), .in1(D_Out_1), .out(multiplexer_4_out), .sel(Swap_R1));
  Multiplexer #(.width(32), .enable("false")) multiplexer_5 (
    .in0(dual_ported_register_file_1_out2), .in1(D_Out_2), .out(multiplexer_5_out), .sel(Swap_R2));
  ID_RR_Buffer id_rr_buffer_1 (
    .Offset_In(bit_extender_1_out), .Data_R1_In(multiplexer_4_out), .Data_R2_In(multiplexer_5_out),
    .Dest_In(multiplexer_3_out), .OpCode_In(id_rr_cntrl_1_opcode_out), .PC_In(fetch_buffer_1_pc_out),
    .Clk_FBuff(Clock), .Offset_Out(Offset), .Data_R1_Out(JALR_PC), .Data_R2_Out(id_rr_buffer_1_data_r2_out),
    .Dest_Out(E_Dest_out), .Opcode_Out(id_rr_buffer_1_opcode_out), .PC_Out(PC_Out), .Flush_In(Flush));
  Multiplexer #(.width(32), .enable("false")) multiplexer_6 (
    .in0(JALR_PC), .in1(Offset), .out(multiplexer_6_out), .sel(Use_IMM));
  Multiplexer #(.width(32), .enable("false")) multiplexer_7 (
    .in0(id_rr_buffer_1_data_r2_out), .in1(PC_Out), .out(multiplexer_7_out), .sel(Use_PC));
  Adder #(.width(32)) adder_1 (.a(Offset), .b(PC_Out), .out(BEQ_PC));  // open: cin, cout
  ALU_Main alu_main_1 (.FUNC(FUNC), .A_In(multiplexer_6_out), .B_In(multiplexer_7_out), .ALU_out(E_ALU_out));
  EX_Cntrl ex_cntrl_1 (
    .Opcode_In(id_rr_buffer_1_opcode_out), .Use_IMM(Use_IMM), .FUNC(FUNC), .Opcode_Out(Ex_Op), .En_Z(En_z),
    .ChkJ(Jump), .FLUSH(Jump_Flush_IT), .Halt(HALT), .Use_PC(Use_PC));
  or or_1 (or_1_out, BEQ_Flush_IT, Jump_Flush_IT);
  Ex_Forwarding_Unit ex_forwarding_unit_1 (
    .ALU_out_In(E_ALU_out), .Dest_In(E_Dest_out), .D_Read_1_In(D_Read_1), .D_Read_2_In(D_Read_2),
    .D_Out_1(D_Out_1_Ex), .D_Out_2(D_Out_2_Ex), .Swap_R1(Swap_R1_Ex), .Swap_R2(Swap_R2_Ex), .Opcode_In(Ex_Op));
  BEQ_Flush beq_flush_1 (.En_z_In(En_z), .chk_z_in(chk_z), .FLUSH_IT_Out(BEQ_Flush_IT));
  Register #(.width(1)) register_1 (.D(or_1_out), .Q(Flush), .clk(Clock), .clr(Flush));  // open: en
  _0 u_0_1 (.Din(E_ALU_out), .En(En_z), .Dout(chk_z));
  EX_Buffer ex_buffer_1 (
    .Rx_In(JALR_PC), .ALU_In(E_ALU_out), .Dest_In(E_Dest_out), .OpCode_In(Ex_Op), .PC_In(PC_Out),
    .Clk_ExBuff(Clock), .Rx_Out(ex_buffer_1_rx_out), .ALU_Out(Mem_ALU_Out), .Dest_Out(Mem_Dest_out),
    .Opcode_Out(ex_buffer_1_opcode_out), .PC_Out(ex_buffer_1_pc_out));
  Data_Mem data_mem_1 (
    .Din(ex_buffer_1_rx_out), .WrMEM(Data_Wr_En), .addr(Mem_ALU_Out), .Clock(Clock), .Dout(Mem_Out),
    .MEM_En(MEM_En));
  MEM_CNTRL mem_cntrl_1 (
    .Opcode_In(ex_buffer_1_opcode_out), .Wr_MEM_out(Data_Wr_En), .Opcode_Out(Mem_Op), .MEM_En(MEM_En));
  MEM_Forwarding_Unit mem_forwarding_unit_1 (
    .ALU_out_In(Mem_ALU_Out), .Dest_In(Mem_Dest_out), .D_Read_1_In(D_Read_1), .D_Read_2_In(D_Read_2),
    .D_Out_1(D_Out_1_Mem), .D_Out_2(D_Out_2_Mem), .Swap_R1(Swap_R1_Mem), .Swap_R2(Swap_R2_Mem),
    .Opcode_In(Mem_Op), .Mem_Out_in(Mem_Out));
  MEM_Buffer mem_buffer_1 (
    .MEM_Out_In(Mem_Out), .ALU_In(Mem_ALU_Out), .Dest_In(Mem_Dest_out), .OpCode_In(Mem_Op),
    .PC_In(ex_buffer_1_pc_out), .Clk_MEM_Buff(Clock), .MEM_Out_out(mem_buffer_1_mem_out_out),
    .ALU_Out(WB_ALU_out), .Dest_Out(Dest_Reg), .Opcode_Out(Wb_Op), .PC_Out(mem_buffer_1_pc_out));
  Multiplexer #(.select(2), .width(32), .enable("false")) multiplexer_8 (
    .in0(WB_ALU_out), .in1(mem_buffer_1_mem_out_out), .in2(mem_buffer_1_pc_out), .out(ToWrite),
    .sel({WB_Sel_1, WB_Sel_0}));  // open: in3
  WB_CNTRL wb_cntrl_1 (.Opcode_In(Wb_Op), .WB_Sel_0(WB_Sel_0), .WB_Sel_1(WB_Sel_1), .WB_En(Reg_WrEn));  // open: sv_PC
  WB_Forwarding_Unit wb_forwarding_unit_1 (
    .ALU_out_In(WB_ALU_out), .Dest_In(Dest_Reg), .D_Read_1_In(D_Read_1), .D_Read_2_In(D_Read_2),
    .D_Out_1(D_Out_1_Wb), .D_Out_2(D_Out_2_Wb), .Swap_R1(Swap_R1_Wb), .Swap_R2(Swap_R2_Wb), .Opcode_In(Wb_Op));
  PC pc_2 ();  // open: Din, Dout, Clk, Clear_PC

  // Other names for the same wires on the sheet: WB_Dest_out[3:0] = Dest_Reg

  // Notes on the sheet:
  //   FETCH
  //   Counter
  //   Imm B15-B0
  //   Rs_B B15-B12
  //   Rs_A B19-B16
  //   Rd
  //   B23-B20
  //   Unused
  //   B25-B24
  //   Opcode B31-B26
  //   Imm
  //   Rs_B
  //   Rs_A
  //   Rd
  //   OpCode
  //   PC
  //   Sign Extend
  //   ID/RR
  //   Dest
  //   OpCode
  //   PC
  //   Data_R2
  //   Dest
  //   Opcode
  //   PC
  //   EX
  //   Data_R1
  //   Data
  //   ALU
  //   Dest
  //   Opcode
  //   PC
  //   MEM
  //   MEM Out
  //   ALU
  //   Dest
  //   Opcode
  //   PC
  //   WB
endmodule

module PC (
  input  [31:0] Din,
  input  Clk,
  input  Clear_PC,
  output [31:0] Dout
);

  Register #(.width(32)) PC (.D(Din), .Q(Dout), .clk(Clk), .clr(Clear_PC));  // open: en
endmodule

// I-MEM
module Instruction_Memory (
  input  [31:0] Din,
  input  Clk,
  input  Clear_IR,
  output [31:0] Dout
);

  RAM #(.addrWidth(24), .dataWidth(32)) ram_1 (
    .addr(Din[23:0]), .data(Dout), .clk(Clk), .ld(1'b1), .clr(Clear_IR));  // open: sel
endmodule

module _1 (
  input  [31:0] Din,
  output [31:0] Dout
);

  Adder #(.width(32)) adder_1 (.a(Din), .b(32'h1), .out(Dout));  // open: cin, cout
endmodule

// FETCH\nBUFFER
module Fetch_Buffer (
  input  [15:0] Offset_In,
  input  [3:0] Rs_B_In,
  input  [3:0] Rs_A_In,
  input  [3:0] Rd_In,
  input  [7:0] OpCode_In,
  input  [31:0] PC_In,
  input  Clk_FBuff,
  input  Flush,
  output [15:0] Offset_Out,
  output [3:0] Rs_B_Out,
  output [3:0] Rs_A_Out,
  output [3:0] Rd_Out,
  output [7:0] Opcode_Out,
  output [31:0] PC_Out
);

  Register #(.width(16)) register_1 (.D(Offset_In), .Q(Offset_Out), .clk(Clk_FBuff), .clr(Flush));  // open: en
  Register #(.width(4)) register_2 (.D(Rs_B_In), .Q(Rs_B_Out), .clk(Clk_FBuff), .clr(Flush));  // open: en
  Register #(.width(4)) register_3 (.D(Rs_A_In), .Q(Rs_A_Out), .clk(Clk_FBuff), .clr(Flush));  // open: en
  Register #(.width(4)) register_4 (.D(Rd_In), .Q(Rd_Out), .clk(Clk_FBuff), .clr(Flush));  // open: en
  Register register_5 (.D(OpCode_In), .Q(Opcode_Out), .clk(Clk_FBuff), .clr(Flush));  // open: en
  Register #(.width(32)) register_6 (.D(PC_In), .Q(PC_Out), .clk(Clk_FBuff), .clr(Flush));  // open: en
endmodule

// ID/RR\nBUFFER
module ID_RR_Buffer (
  input  [31:0] Offset_In,
  input  [31:0] Data_R1_In,
  input  [31:0] Data_R2_In,
  input  [3:0] Dest_In,
  input  [7:0] OpCode_In,
  input  [31:0] PC_In,
  input  Clk_FBuff,
  input  Flush_In,
  output [31:0] Offset_Out,
  output [31:0] Data_R1_Out,
  output [31:0] Data_R2_Out,
  output [3:0] Dest_Out,
  output [7:0] Opcode_Out,
  output [31:0] PC_Out
);

  Register #(.width(32)) register_1 (.D(Offset_In), .Q(Offset_Out), .clk(Clk_FBuff), .clr(Flush_In));  // open: en
  Register #(.width(32)) register_2 (.D(Data_R1_In), .Q(Data_R1_Out), .clk(Clk_FBuff), .clr(Flush_In));  // open: en
  Register #(.width(32)) register_3 (.D(Data_R2_In), .Q(Data_R2_Out), .clk(Clk_FBuff), .clr(Flush_In));  // open: en
  Register #(.width(4)) register_4 (.D(Dest_In), .Q(Dest_Out), .clk(Clk_FBuff), .clr(Flush_In));  // open: en
  Register register_5 (.D(OpCode_In), .Q(Opcode_Out), .clk(Clk_FBuff), .clr(Flush_In));  // open: en
  Register #(.width(32)) register_6 (.D(PC_In), .Q(PC_Out), .clk(Clk_FBuff), .clr(Flush_In));  // open: en
endmodule

// ALU\nMain
module ALU_Main (
  input  [31:0] A_In,
  input  [31:0] B_In,
  input  [1:0] FUNC,
  output [31:0] ALU_out
);

  wire [31:0] adder_1_out, nand_1_out, subtractor_1_out;

  Adder #(.width(32)) adder_1 (.a(A_In), .b(B_In), .out(adder_1_out));  // open: cin, cout
  assign nand_1_out = ~(A_In & B_In);  // NAND_Gate nand_1, 32 bits wide
  Multiplexer #(.select(2), .width(32), .enable("false")) multiplexer_1 (
    .in0(adder_1_out), .in1(nand_1_out), .in2(subtractor_1_out), .in3(A_In), .out(ALU_out), .sel(FUNC));
  Subtractor #(.width(32)) subtractor_1 (.a(A_In), .b(B_In), .out(subtractor_1_out));  // open: bin, bout
endmodule

// EX\nBUFFER
module EX_Buffer (
  input  [31:0] Rx_In,
  input  [31:0] ALU_In,
  input  [3:0] Dest_In,
  input  [7:0] OpCode_In,
  input  [31:0] PC_In,
  input  Clk_ExBuff,
  output [31:0] Rx_Out,
  output [31:0] ALU_Out,
  output [3:0] Dest_Out,
  output [7:0] Opcode_Out,
  output [31:0] PC_Out
);

  Register #(.width(32)) register_1 (.D(Rx_In), .Q(Rx_Out), .clk(Clk_ExBuff));  // open: en, clr
  Register #(.width(32)) register_2 (.D(ALU_In), .Q(ALU_Out), .clk(Clk_ExBuff));  // open: en, clr
  Register #(.width(4)) register_3 (.D(Dest_In), .Q(Dest_Out), .clk(Clk_ExBuff));  // open: en, clr
  Register register_4 (.D(OpCode_In), .Q(Opcode_Out), .clk(Clk_ExBuff));  // open: en, clr
  Register #(.width(32)) register_5 (.D(PC_In), .Q(PC_Out), .clk(Clk_ExBuff));  // open: en, clr
endmodule

// Ex\nCNTRL
module EX_Cntrl (
  input  [7:0] Opcode_In,
  output Halt,
  output Use_PC,
  output Use_IMM,
  output [1:0] FUNC,
  output En_Z,
  output ChkJ,
  output FLUSH,
  output [7:0] Opcode_Out
);

  and and_1 (Halt, Opcode_In[3], Opcode_In[4], Opcode_In[5], Opcode_In[6], Opcode_In[7]);

  assign ChkJ = Opcode_In[0];
  assign En_Z = Opcode_In[1];
  assign FLUSH = Opcode_In[0];
  assign FUNC = Opcode_In[5:4];
  assign Opcode_Out = Opcode_In;
  assign Use_IMM = Opcode_In[6];
  assign Use_PC = Opcode_In[7];

  // Notes on the sheet:
  //   Halt Logic
  //   MEM
endmodule

// =0?
module _0 (
  input  [31:0] Din,
  input  En,
  output Dout
);

  wire and_1_out, and_2_out, and_3_out, nor_1_out, nor_2_out, nor_3_out, nor_4_out, nor_5_out, nor_6_out,
       nor_7_out, nor_8_out;

  nor nor_1 (nor_1_out, Din[0], Din[1], Din[2], Din[3]);
  nor nor_2 (nor_2_out, Din[4], Din[5], Din[6], Din[7]);
  nor nor_3 (nor_3_out, Din[8], Din[9], Din[10], Din[11]);
  nor nor_4 (nor_4_out, Din[12], Din[13], Din[14], Din[15]);
  nor nor_5 (nor_5_out, Din[20], Din[21], Din[22], Din[23]);
  nor nor_6 (nor_6_out, Din[24], Din[25], Din[26], Din[27]);
  nor nor_7 (nor_7_out, Din[28], Din[29], Din[30], Din[31]);
  nor nor_8 (nor_8_out, Din[16], Din[17], Din[18], Din[19]);
  and and_1 (and_1_out, nor_1_out, nor_2_out, nor_3_out, nor_4_out);
  and and_2 (and_2_out, nor_8_out, nor_5_out, nor_6_out, nor_7_out);
  and and_3 (and_3_out, and_1_out, and_2_out);
  and and_4 (Dout, and_3_out, En);
endmodule

// ID/RR\nCNTRL
module ID_RR_Cntrl (
  input  [7:0] Opcode_In,
  output Read_Rd,
  output Dest_Rs_A,
  output [7:0] Opcode_Out
);

  wire and_1_out;

  and and_1 (and_1_out, Opcode_In[3], Opcode_In[6]);
  or or_1 (Read_Rd, and_1_out, Opcode_In[1], Opcode_In[0]);

  assign Dest_Rs_A = Opcode_In[0];
  assign Opcode_Out = Opcode_In;

  // Notes on the sheet:
  //   SW_Logic
  //   BEQ_Logic
  //   JALR_Logic
endmodule

module BEQ_Flush (
  input  En_z_In,
  input  chk_z_in,
  output FLUSH_IT_Out
);

  and and_1 (FLUSH_IT_Out, En_z_In, chk_z_in);
endmodule

// Data_MEM
module Data_Mem (
  input  [31:0] Din,
  input  WrMEM,
  input  [31:0] addr,
  input  Clock,
  input  MEM_En,
  output [31:0] Dout
);

  wire not_1_out;

  assign Dout = WrMEM ? Din : 32'bz;  // Controlled_Buffer controlled_buffer_1
  not not_1 (not_1_out, WrMEM);
  RAM #(.addrWidth(24), .dataWidth(32)) ram_1 (
    .addr(addr[23:0]), .data(Dout), .sel(MEM_En), .clk(Clock), .ld(not_1_out));  // open: clr
endmodule

// MEM\nCNTRL
module MEM_CNTRL (
  input  [7:0] Opcode_In,
  output MEM_En,
  output Wr_MEM_out,
  output [7:0] Opcode_Out
);


  assign MEM_En = Opcode_In[2];
  assign Opcode_Out = Opcode_In;
  assign Wr_MEM_out = Opcode_In[3];
endmodule

// MEM\nBUFFER
module MEM_Buffer (
  input  [31:0] MEM_Out_In,
  input  [31:0] ALU_In,
  input  [3:0] Dest_In,
  input  [7:0] OpCode_In,
  input  [31:0] PC_In,
  input  Clk_MEM_Buff,
  output [31:0] MEM_Out_out,
  output [31:0] ALU_Out,
  output [3:0] Dest_Out,
  output [7:0] Opcode_Out,
  output [31:0] PC_Out
);

  Register #(.width(32)) register_1 (.D(MEM_Out_In), .Q(MEM_Out_out), .clk(Clk_MEM_Buff));  // open: en, clr
  Register #(.width(32)) register_2 (.D(ALU_In), .Q(ALU_Out), .clk(Clk_MEM_Buff));  // open: en, clr
  Register #(.width(4)) register_3 (.D(Dest_In), .Q(Dest_Out), .clk(Clk_MEM_Buff));  // open: en, clr
  Register register_4 (.D(OpCode_In), .Q(Opcode_Out), .clk(Clk_MEM_Buff));  // open: en, clr
  Register #(.width(32)) register_5 (.D(PC_In), .Q(PC_Out), .clk(Clk_MEM_Buff));  // open: en, clr
endmodule

// WB\nCNTRL
module WB_CNTRL (
  input  [7:0] Opcode_In,
  output WB_Sel_0,
  output WB_Sel_1,
  output sv_PC,
  output WB_En
);

  wire and_1_out;

  and and_1 (and_1_out, Opcode_In[2], Opcode_In[3]);
  nor nor_1 (WB_En, and_1_out, Opcode_In[1]);

  assign sv_PC = Opcode_In[0];
  assign WB_Sel_0 = Opcode_In[2];
  assign WB_Sel_1 = Opcode_In[3];

  // Notes on the sheet:
  //   SW Logic
  //   BEQ Logic
endmodule

// Ex\nForwarding\nUnit
module Ex_Forwarding_Unit (
  input  [31:0] ALU_out_In,
  input  [3:0] Dest_In,
  input  [3:0] D_Read_1_In,
  input  [3:0] D_Read_2_In,
  input  [7:0] Opcode_In,
  output [31:0] D_Out_1,
  output [31:0] D_Out_2,
  output Swap_R1,
  output Swap_R2
);

  wire and_1_out, and_2_out, and_3_out, nor_1_out, nor_2_out, nor_3_out, nor_4_out, nor_5_out;
  wire [3:0] subtractor_1_out, subtractor_2_out;

  Subtractor #(.width(4)) subtractor_1 (.a(Dest_In), .b(D_Read_1_In), .out(subtractor_1_out));  // open: bin, bout
  Subtractor #(.width(4)) subtractor_2 (.a(Dest_In), .b(D_Read_2_In), .out(subtractor_2_out));  // open: bin, bout
  nor nor_1 (nor_1_out, subtractor_1_out[0], subtractor_1_out[1]);
  nor nor_2 (nor_2_out, subtractor_1_out[2], subtractor_1_out[3]);
  nor nor_3 (nor_3_out, subtractor_2_out[0], subtractor_2_out[1]);
  nor nor_4 (nor_4_out, subtractor_2_out[2], subtractor_2_out[3]);
  and and_1 (and_1_out, nor_3_out, nor_4_out);
  and and_2 (and_2_out, Opcode_In[3], Opcode_In[2]);
  and and_3 (and_3_out, nor_1_out, nor_2_out);
  and and_4 (Swap_R2, and_1_out, nor_5_out);
  nor nor_5 (nor_5_out, and_2_out, Opcode_In[1]);
  and and_5 (Swap_R1, and_3_out, nor_5_out);

  assign D_Out_1 = ALU_out_In;
  assign D_Out_2 = ALU_out_In;

  // Notes on the sheet:
  //   Is a D_Read Reg the same as a E_Dest Reg (RAW)?
  //   Make sure the op is a writing operation (not beq or sw)
endmodule

// MEM\nFordwarding\nUnit
module MEM_Forwarding_Unit (
  input  [31:0] ALU_out_In,
  input  [31:0] Mem_Out_in,
  input  [3:0] Dest_In,
  input  [3:0] D_Read_1_In,
  input  [3:0] D_Read_2_In,
  input  [7:0] Opcode_In,
  output [31:0] D_Out_1,
  output [31:0] D_Out_2,
  output Swap_R1,
  output Swap_R2
);

  wire and_1_out, and_2_out, and_3_out, and_6_out, nor_1_out, nor_2_out, nor_3_out, nor_4_out, nor_5_out,
       not_1_out;
  wire [3:0] subtractor_1_out, subtractor_2_out;

  Multiplexer #(.width(32), .enable("false")) multiplexer_1 (
    .in0(ALU_out_In), .in1(Mem_Out_in), .out(D_Out_1), .sel(and_6_out));
  Subtractor #(.width(4)) subtractor_1 (.a(Dest_In), .b(D_Read_1_In), .out(subtractor_1_out));  // open: bin, bout
  Subtractor #(.width(4)) subtractor_2 (.a(Dest_In), .b(D_Read_2_In), .out(subtractor_2_out));  // open: bin, bout
  nor nor_1 (nor_1_out, subtractor_1_out[0], subtractor_1_out[1]);
  nor nor_2 (nor_2_out, subtractor_1_out[2], subtractor_1_out[3]);
  nor nor_3 (nor_3_out, subtractor_2_out[0], subtractor_2_out[1]);
  nor nor_4 (nor_4_out, subtractor_2_out[2], subtractor_2_out[3]);
  and and_1 (and_1_out, nor_3_out, nor_4_out);
  and and_2 (and_2_out, Opcode_In[3], Opcode_In[2]);
  and and_3 (and_3_out, nor_1_out, nor_2_out);
  not not_1 (not_1_out, Opcode_In[3]);
  and and_4 (Swap_R1, and_3_out, nor_5_out);
  and and_5 (Swap_R2, and_1_out, nor_5_out);
  nor nor_5 (nor_5_out, and_2_out, Opcode_In[1]);
  and and_6 (and_6_out, not_1_out, Opcode_In[2]);

  assign D_Out_2 = D_Out_1;

  // Notes on the sheet:
  //   Is a D_Read Reg the same as a E_Dest Reg (RAW)?
  //   If LW then forward Mem out
  //   Make sure the op is a writing operation (not beq or sw)
  //   Check if LW 
endmodule

// WB\nFordwarding\nUnit
module WB_Forwarding_Unit (
  input  [31:0] ALU_out_In,
  input  [3:0] Dest_In,
  input  [3:0] D_Read_1_In,
  input  [3:0] D_Read_2_In,
  input  [7:0] Opcode_In,
  output [31:0] D_Out_1,
  output [31:0] D_Out_2,
  output Swap_R1,
  output Swap_R2
);

  wire and_1_out, and_2_out, and_3_out, nor_1_out, nor_2_out, nor_3_out, nor_4_out, nor_5_out;
  wire [3:0] subtractor_1_out, subtractor_2_out;

  Subtractor #(.width(4)) subtractor_1 (.a(Dest_In), .b(D_Read_1_In), .out(subtractor_1_out));  // open: bin, bout
  Subtractor #(.width(4)) subtractor_2 (.a(Dest_In), .b(D_Read_2_In), .out(subtractor_2_out));  // open: bin, bout
  nor nor_1 (nor_1_out, subtractor_1_out[0], subtractor_1_out[1]);
  nor nor_2 (nor_2_out, subtractor_1_out[2], subtractor_1_out[3]);
  nor nor_3 (nor_3_out, subtractor_2_out[0], subtractor_2_out[1]);
  nor nor_4 (nor_4_out, subtractor_2_out[2], subtractor_2_out[3]);
  and and_1 (and_1_out, Opcode_In[3], Opcode_In[2]);
  and and_2 (and_2_out, nor_3_out, nor_4_out);
  and and_3 (and_3_out, nor_1_out, nor_2_out);
  nor nor_5 (nor_5_out, and_1_out, Opcode_In[1]);
  and and_4 (Swap_R1, and_3_out, nor_5_out);
  and and_5 (Swap_R2, and_2_out, nor_5_out);

  assign D_Out_1 = ALU_out_In;
  assign D_Out_2 = ALU_out_In;

  // Notes on the sheet:
  //   Is a D_Read Reg the same as a E_Dest Reg (RAW)?
  //   Make sure the op is a writing operation (not beq or sw)
endmodule

// Master\nForwarding\nUnit
module Master_Forwarding_Unit (
  input  Forward_WB_1_In,
  input  Forward_MEM_1_In,
  input  Forward_EX_1_In,
  input  [31:0] WB_D_1,
  input  [31:0] MEM_D_1,
  input  [31:0] EX_D_1,
  input  Forward_WB_2_In,
  input  Forward_MEM_2_In,
  input  Forward_EX_2_In,
  input  [31:0] WB_D_2,
  input  [31:0] MEM_D_2,
  input  [31:0] EX_D_2,
  output Swap_R1,
  output [31:0] D_1_Out,
  output Swap_R2,
  output [31:0] D_2_Out
);

  wire not_1_out, not_2_out, priority_encoder_1_en_out, priority_encoder_2_en_out;
  wire [1:0] priority_encoder_1_out, priority_encoder_2_out;
  wire [2:0] decoder_1_out0, decoder_2_out0;

  not not_1 (not_1_out, priority_encoder_1_en_out);
  Decoder #(.select(2), .disabled(0)) decoder_1 (
    .out0(decoder_1_out0[0]), .out1(decoder_1_out0[1]), .out2(decoder_1_out0[2]),
    .sel(priority_encoder_1_out), .en(not_1_out));  // open: out3
  Priority_Encoder #(.select(2), .disabled(0)) priority_encoder_1 (
    .in0(Forward_WB_1_In), .in1(Forward_MEM_1_In), .in2(Forward_EX_1_In), .in3(1'b0),
    .out(priority_encoder_1_out), .en_out(priority_encoder_1_en_out));  // open: gs, en_in
  not not_2 (not_2_out, priority_encoder_2_en_out);
  Priority_Encoder #(.select(2), .disabled(0)) priority_encoder_2 (
    .in0(Forward_WB_2_In), .in1(Forward_MEM_2_In), .in2(Forward_EX_2_In), .in3(1'b0),
    .out(priority_encoder_2_out), .en_out(priority_encoder_2_en_out));  // open: gs, en_in
  Decoder #(.select(2), .disabled(0)) decoder_2 (
    .out0(decoder_2_out0[0]), .out1(decoder_2_out0[1]), .out2(decoder_2_out0[2]),
    .sel(priority_encoder_2_out), .en(not_2_out));  // open: out3
  Multiplexer #(.select(3), .width(32), .enable("false")) multiplexer_1 (
    .in1(WB_D_1), .in2(MEM_D_1), .in4(EX_D_1), .out(D_1_Out), .sel(decoder_1_out0));  // open: in0, in3, in5, in6, in7
  or or_1 (Swap_R2, decoder_2_out0[0], decoder_2_out0[2], decoder_2_out0[1]);
  Multiplexer #(.select(3), .width(32), .enable("false")) multiplexer_2 (
    .in1(WB_D_2), .in2(MEM_D_2), .in4(EX_D_2), .out(D_2_Out), .sel(decoder_2_out0));  // open: in0, in3, in5, in6, in7
  or or_2 (Swap_R1, decoder_1_out0[0], decoder_1_out0[2], decoder_1_out0[1]);
endmodule
